# Fritzing sketch NanoAndNanoESP32_1 (saved by Fritzing 1.0.5)
circuit board: 7.6cm x 5cm
breadboards: 1

parts:
  Nano = Arduino Nano (Rev3.0)
  5V = male pin header, 8 pins [form="♂ (male)"]
  GND = male pin header, 8 pins [form="♂ (male)"]
  3V3 = male pin header, 8 pins [form="♂ (male)"]
  SDA = male pin header, 6 pins [form="♂ (male)"]
  SCL = male pin header, 6 pins [form="♂ (male)"]
  S = male pin header, 2 pins [form="♂ (male)"]
  A2 = male pin header, 6 pins [form="♂ (male)"]
  D2 = female pin header, 12 pins [form="♀ (female)"]
  Nano_ESP32 = Arduino Nano (Rev3.0)
  D1 = female pin header, 12 pins [form="♀ (female)"]
  J1 = Screw terminal - 2 pins [package=THT]

nets:
  N1: Nano.D1/TX, S.pin2, Nano_ESP32.D9, D1.pin8
  N2: Nano.D0/RX, S.pin1, Nano_ESP32.D10, D1.pin9
  GND: Nano.GND, GND.pin1, GND.pin2, GND.pin3, GND.pin4, GND.pin5, GND.pin6, GND.pin7, GND.pin8, Nano_ESP32.GND, J1.pin1
  N3: Nano.D2, D2.pin1
  N4: Nano.D3, D2.pin2
  N5: Nano.D4, D2.pin3
  N6: Nano.D5, D2.pin4
  N7: Nano.D6, D2.pin5
  N8: Nano.D7, D2.pin6
  N9: Nano.D8, D2.pin7
  N10: Nano.D9, D2.pin8
  N11: Nano.D10, D2.pin9
  N12: Nano.D11/MOSI, D2.pin10
  N13: Nano.D12/MISO, D2.pin11
  VIN: Nano.VIN, 5V.pin1, 5V.pin2, 5V.pin3, 5V.pin4, 5V.pin5, 5V.pin6, 5V.pin7, 5V.pin8, Nano_ESP32.VIN, J1.pin2
  N14: Nano.A7, A2.pin1
  N15: Nano.A6, A2.pin2
  N16: Nano.A5, SCL.pin1, SCL.pin2, SCL.pin3, SCL.pin4, SCL.pin5, SCL.pin6
  N17: Nano.A4, SDA.pin1, SDA.pin2, SDA.pin3, SDA.pin4, SDA.pin5, SDA.pin6
  N18: Nano.A3, A2.pin3
  N19: Nano.A2, A2.pin4
  N20: Nano.A1, A2.pin5
  N21: Nano.A0, A2.pin6
  N22: Nano.3V3, 3V3.pin1, 3V3.pin2, 3V3.pin3, 3V3.pin4, 3V3.pin5, 3V3.pin6, 3V3.pin7, 3V3.pin8
  N23: Nano.D13/SCK, D2.pin12
  N24: Nano_ESP32.D2, D1.pin1
  N25: Nano_ESP32.D3, D1.pin2
  N26: Nano_ESP32.D4, D1.pin3
  N27: Nano_ESP32.D5, D1.pin4
  N28: Nano_ESP32.D6, D1.pin5
  N29: Nano_ESP32.D7, D1.pin6
  N30: Nano_ESP32.D8, D1.pin7
  N31: Nano_ESP32.D11/MOSI, D1.pin10
  N32: Nano_ESP32.D12/MISO, D1.pin11
  N33: Nano_ESP32.D13/SCK, D1.pin12
