# Fritzing sketch NanoBasic3 (saved by Fritzing 1.0.5)
circuit board: 5cm x 5cm
breadboards: 1

parts:
  Arduino_Nano = Arduino Nano (Rev3.0)
  5V = male pin header, 8 pins [form="♂ (male)"]
  GND = male pin header, 8 pins [form="♂ (male)"]
  3V3 = male pin header, 8 pins [form="♂ (male)"]
  SDA = male pin header, 6 pins [form="♂ (male)"]
  SCL = male pin header, 6 pins [form="♂ (male)"]
  S = male pin header, 2 pins [form="♂ (male)"]
  A = male pin header, 6 pins [form="♂ (male)"]
  D = female pin header, 12 pins [form="♀ (female)"]

nets:
  N1: Arduino_Nano.D1/TX, S.pin2
  N2: Arduino_Nano.D0/RX, S.pin1
  N3: Arduino_Nano.GND, GND.pin1, GND.pin2, GND.pin3, GND.pin4, GND.pin5, GND.pin6, GND.pin7, GND.pin8
  N4: Arduino_Nano.D2, D.pin1
  N5: Arduino_Nano.D3, D.pin2
  N6: Arduino_Nano.D4, D.pin3
  N7: Arduino_Nano.D5, D.pin4
  N8: Arduino_Nano.D6, D.pin5
  N9: Arduino_Nano.D7, D.pin6
  N10: Arduino_Nano.D8, D.pin7
  N11: Arduino_Nano.D9, D.pin8
  N12: Arduino_Nano.D10, D.pin9
  N13: Arduino_Nano.D11/MOSI, D.pin10
  N14: Arduino_Nano.D12/MISO, D.pin11
  N15: Arduino_Nano.VIN, 5V.pin1, 5V.pin2, 5V.pin3, 5V.pin4, 5V.pin5, 5V.pin6, 5V.pin7, 5V.pin8
  N16: Arduino_Nano.A7, A.pin1
  N17: Arduino_Nano.A6, A.pin2
  N18: Arduino_Nano.A5, SCL.pin1, SCL.pin2, SCL.pin3, SCL.pin4, SCL.pin5, SCL.pin6
  N19: Arduino_Nano.A4, SDA.pin1, SDA.pin2, SDA.pin3, SDA.pin4, SDA.pin5, SDA.pin6
  N20: Arduino_Nano.A3, A.pin3
  N21: Arduino_Nano.A2, A.pin4
  N22: Arduino_Nano.A1, A.pin5
  N23: Arduino_Nano.A0, A.pin6
  N24: Arduino_Nano.3V3, 3V3.pin1, 3V3.pin2, 3V3.pin3, 3V3.pin4, 3V3.pin5, 3V3.pin6, 3V3.pin7, 3V3.pin8
  N25: Arduino_Nano.D13/SCK, D.pin12
