# Fritzing sketch PowerSupply5V_V2.1 (saved by Fritzing 0.9.9b)
circuit board: 7cm x 5cm
breadboards: 1

parts:
  U1 = Voltage Regulator - 5V [package="TO220 [THT]"]
  C1 = Ceramic Capacitor [capacitance=100nF voltage=35V package="100 mil [THT, multilayer]"]
  C2 = Ceramic Capacitor [capacitance=100nF voltage=35V package="100 mil [THT, multilayer]"]
  U2 = Voltage Regulator - 5V [package="TO220 [THT]"]
  U3 = Voltage Regulator - 5V [package="TO220 [THT]"]
  U4 = Voltage Regulator - 5V [package="TO220 [THT]"]
  U5 = Voltage Regulator - 5V [package="TO220 [THT]"]
  U6 = Voltage Regulator - 5V [package="TO220 [THT]"]
  U7 = Voltage Regulator - 5V [package="TO220 [THT]"]
  U8 = Voltage Regulator - 5V [package="TO220 [THT]"]
  J1 = Screw terminal - 2 pins [package=THT]
  J2 = Screw terminal - 2 pins [package=THT]
  LED1 = LED - 5mm [color="Red (633nm)" current=0.030 package="5 mm [THT]"]
  R1 = Resistor [tolerance=±5% power=0.25 resistance=220 package=THT]

nets:
  N1: U1.input_voltage, C2.1, U2.input_voltage, U3.input_voltage, U4.input_voltage, U5.input_voltage, U6.input_voltage, U7.input_voltage, U8.input_voltage, J1.pin2
  GND: U1.GND, C1.0, C2.0, U2.GND, U3.GND, U4.GND, U5.GND, U6.GND, U7.GND, U8.GND, J1.pin1, J2.pin2, R1.Pin_1
  N2: U1.output_voltage, C1.1, U2.output_voltage, U3.output_voltage, U4.output_voltage, U5.output_voltage, U6.output_voltage, U7.output_voltage, U8.output_voltage, J2.pin1, LED1.anode
  N3: LED1.cathode, R1.Pin_0

notes:
  VIN
  GND
  VOUT
  beCeeSoftArt - Constant Power v2.1
